// Logisim project ProiectPSN.circ as structural Verilog
module main (
  input  Input_1,
  input  Input_2,
  input  Input_3,
  input  clk,
  output [3:0] anod,
  output [6:0] catod
);

  wire ADMIN_out, bis_d_1_q, clk_div_1_clk_out, compartor_1_eg, confirm_out, deb_3_1_y, deb_3_2_y, not_1_out,
       reg_1_v_out, t_ff_1_q, uc_1_en1, uc_1_en2, uc_1_en3, uc_1_sel;
  wire [3:0] numarator4_1_q, numarator4_2_q, numarator4_3_q;
  wire [15:0] concanator_2_output_reg, dmux_2_1_out0, dmux_2_1_out1, multiplexer_1_out, reg_admin_1_v_out,
       reg_mare_1_v_out, reg_mare_2_v_out;

  DEB_3 deb_3_1 (.CLK(clk), .B(ADMIN_out), .Y(deb_3_1_y));
  Button ADMIN (.out(ADMIN_out));
  Button confirm (.out(confirm_out));
  DEB_3 deb_3_2 (.CLK(clk), .B(confirm_out), .Y(deb_3_2_y));
  BIS_D bis_d_1 (.CLK(clk), .D(uc_1_sel), .Q(bis_d_1_q));
  UC uc_1 (
    .ADMIN(deb_3_1_y), .CIF1(Input_1), .CIF2(Input_2), .CIF3(Input_3), .CONFIRM(deb_3_2_y), .CLK(clk),
    .SEL(uc_1_sel), .EN1(uc_1_en1), .EN2(uc_1_en2), .EN3(uc_1_en3));
  clk_div clk_div_1 (.clk(clk), .clk_out(clk_div_1_clk_out));
  REG reg_1 (.V_IN(uc_1_sel), .RST(compartor_1_eg), .CLK(clk), .V_OUT(reg_1_v_out));
  NUMARATOR4 numarator4_1 (.CLK(clk_div_1_clk_out), .RST(bis_d_1_q), .EN(uc_1_en1), .Q(numarator4_1_q));
  NUMARATOR4 numarator4_2 (.CLK(clk_div_1_clk_out), .RST(bis_d_1_q), .EN(uc_1_en2), .Q(numarator4_2_q));
  NUMARATOR4 numarator4_3 (.CLK(clk_div_1_clk_out), .RST(bis_d_1_q), .EN(uc_1_en3), .Q(numarator4_3_q));
  LED ADMIN_ON (.in(t_ff_1_q));
  LED locked (.in(reg_1_v_out));
  ssd16 ssd16_1 (
    .clock_100Mhz(clk), .reset(uc_1_sel), .data(concanator_2_output_reg), .Anode_Activate(anod),
    .LED_out(catod));
  not not_1 (not_1_out, deb_3_2_y);
  concanator concanator_2 (
    .REG1(numarator4_1_q), .REG2(numarator4_2_q), .REG3(numarator4_3_q), .CLK(clk),
    .OUTPUT_REG(concanator_2_output_reg));
  T_FF t_ff_1 (.T(deb_3_1_y), .RST(compartor_1_eg), .Q(t_ff_1_q));
  REG_ADMIN reg_admin_1 (.V_OUT(reg_admin_1_v_out));
  DMUX_2 dmux_2_1 (.intr(concanator_2_output_reg), .sel(reg_1_v_out), .out0(dmux_2_1_out0), .out1(dmux_2_1_out1));
  REG_MARE reg_mare_1 (.V_IN(dmux_2_1_out0), .EN(not_1_out), .CLK(clk), .V_OUT(reg_mare_1_v_out));
  REG_MARE reg_mare_2 (.V_IN(dmux_2_1_out1), .EN(not_1_out), .CLK(clk), .V_OUT(reg_mare_2_v_out));
  Multiplexer #(.width(16)) multiplexer_1 (
    .in0(reg_mare_1_v_out), .in1(reg_admin_1_v_out), .out(multiplexer_1_out), .sel(t_ff_1_q));
  COMPARTOR compartor_1 (
    .IN1(reg_mare_2_v_out), .IN2(multiplexer_1_out), .EN(deb_3_2_y), .CLK(clk), .EG(compartor_1_eg));
endmodule

// VHDL entity REGISTRU, as the project stores it:
LIBRARY ieee;
USE ieee.std_logic_1164.all;

ENTITY REGISTRU IS
  PORT (
  	V_IN : IN STD_LOGIC_VECTOR(3 DOWNTO 0);
  	CLK : IN STD_LOGIC;
  	V_OUT : OUT STD_LOGIC_VECTOR(3 DOWNTO 0)
    );
END REGISTRU;

ARCHITECTURE TypeArchitecture OF REGISTRU IS
	SIGNAL V_INT : STD_LOGIC_VECTOR(3 DOWNTO 0);
BEGIN
	PROCESS(CLK)
	BEGIN
	IF RISING_EDGE(CLK) THEN 
		V_INT <=  V_IN;
	END IF;  
	END PROCESS;
	V_OUT <= V_INT;
END TypeArchitecture;

// VHDL entity NUMARATOR2, as the project stores it:
LIBRARY ieee;
USE ieee.std_logic_1164.all;
USE ieee.std_logic_unsigned.all;

ENTITY NUMARATOR2 IS
  PORT (
  	CLK, RST, EN : IN STD_LOGIC;
  	Q : OUT STD_LOGIC_VECTOR( 1 DOWNTO 0);
  	COUT : OUT STD_LOGIC
    );
END NUMARATOR2;


ARCHITECTURE TypeArchitecture OF NUMARATOR2 IS

BEGIN
	PROCESS(CLK,RST,EN)
	VARIABLE NR: STD_LOGIC_VECTOR(1 DOWNTO 0):=(OTHERS => '0');
	BEGIN
		IF RST='1' THEN NR:=(OTHERS => '0');
		ELSIF RISING_EDGE( CLK ) THEN
			IF EN = '1' THEN 
			 	NR:= NR+1;
			END IF;
		END IF;
		Q <= NR;
		IF NR = "11" THEN
		COUT <= '1';
		ELSE COUT <= '0';
		END IF;
	END PROCESS;

END TypeArchitecture;

// VHDL entity DMUX1_4, as the project stores it:
library IEEE;
use IEEE.STD_LOGIC_1164.ALL;

entity DMUX1_4 is
 port(
 		out0, out1, out2, out3:out std_logic_vector(3 downto 0);
       intr:in std_logic_vector(3 downto 0);
       sel:in std_logic_vector(1 downto 0)
       );
end DMUX1_4;

architecture Behavioral of DMUX1_4 is

begin
	process(intr,sel)
    begin
    if(sel="00")then out0<=intr; --out1 <= "0000"; out2 <= "0000"; out3 <= "0000";
    elsif(sel="01")then out1<=intr; --out0<= "0000"; out2 <= "0000"; out3 <= "0000";
    elsif(sel="10")then out2<=intr; --out0 <= "0000"; out1 <= "0000"; out3 <= "0000";
    elsif(sel="11")then out3<=intr; --out0 <= "0000"; out1 <= "0000"; out2 <= "0000";
  end if;    
    end process;
end Behavioral;

// VHDL entity COMPARTOR, as the project stores it:
LIBRARY ieee;
USE ieee.std_logic_1164.all;
USE ieee.std_logic_unsigned.all;

ENTITY COMPARTOR IS
  PORT (
	IN1, IN2 : IN STD_LOGIC_VECTOR( 15 DOWNTO 0);
	EN : IN STD_LOGIC;
	CLK : IN STD_LOGIC;
	EG : OUT STD_LOGIC
    );
END COMPARTOR;


ARCHITECTURE TypeArchitecture OF COMPARTOR IS

BEGIN
	PROCESS(EN,CLK)
	BEGIN 
	IF RISING_EDGE( CLK) THEN
	IF EN = '1' THEN 
		IF IN1 = IN2 THEN
			EG <= '1';
			END IF;
		ELSE EG <='0';
	END IF;
	END IF;	
	END PROCESS;

END TypeArchitecture;

// VHDL entity PmodKYPD, as the project stores it:
----------------------------------------------------------------------------------
-- Company: Digilent Inc 2011
-- Engineer: Michelle Yu  
-- Create Date:    17:05:39 08/23/2011 
--
-- Module Name:    PmodKYPD - Behavioral 
-- Project Name:  PmodKYPD
-- Target Devices: Nexys3
-- Tool versions: Xilinx ISE 13.2 
-- Description: 
--	This file defines a project that outputs the key pressed on the PmodKYPD to the seven segment display
--
-- Revision: 
-- Revision 0.01 - File Created
----------------------------------------------------------------------------------
library IEEE;
use IEEE.STD_LOGIC_1164.ALL;
use IEEE.STD_LOGIC_ARITH.ALL;
use IEEE.STD_LOGIC_UNSIGNED.ALL;

entity PmodKYPD is
    Port ( 
			  clk : in  STD_LOGIC;
			  JA : inout  STD_LOGIC_VECTOR (7 downto 0); -- PmodKYPD is designed to be connected to JA
         data: out std_logic_vector(3 downto 0));
end PmodKYPD;

architecture Behavioral of PmodKYPD is

component Decoder is
	Port (
			 clk : in  STD_LOGIC;
          Row : in  STD_LOGIC_VECTOR (3 downto 0);
			 Col : out  STD_LOGIC_VECTOR (3 downto 0);
          DecodeOut : out  STD_LOGIC_VECTOR (3 downto 0));
	end component;
signal Decode: STD_LOGIC_VECTOR (3 downto 0);
begin

	
	C0: Decoder port map (clk=>clk, Row =>JA(7 downto 4), Col=>JA(3 downto 0), DecodeOut=> data);


end Behavioral;

----------------------------------------------------------------------------------
-- Company: Digilent Inc 2011
-- Engineer: Michelle Yu  
-- Create Date:      17:18:24 08/23/2011 
--
-- Module Name:    Decoder - Behavioral 
-- Project Name:  PmodKYPD
-- Target Devices: Nexys3
-- Tool versions: Xilinx ISE 13.2
-- Description: 
--	This file defines a component Decoder for the demo project PmodKYPD. 
-- The Decoder scans each column by asserting a low to the pin corresponding to the column 
-- at 1KHz. After a column is asserted low, each row pin is checked. 
-- When a row pin is detected to be low, the key that was pressed could be determined.
--
-- Revision: 
-- Revision 0.01 - File Created
----------------------------------------------------------------------------------
library IEEE;
use IEEE.STD_LOGIC_1164.ALL;
use IEEE.STD_LOGIC_ARITH.ALL;
use IEEE.STD_LOGIC_UNSIGNED.ALL;

entity Decoder is
    Port (
			  clk : in  STD_LOGIC;
          Row : in  STD_LOGIC_VECTOR (3 downto 0);
			 Col : out  STD_LOGIC_VECTOR (3 downto 0);
          DecodeOut : out  STD_LOGIC_VECTOR (3 downto 0));
end Decoder;

architecture Behavioral of Decoder is

signal sclk :STD_LOGIC_VECTOR(19 downto 0);
begin
	process(clk)
		begin 
		if clk'event and clk = '1' then
			-- 1ms
			if sclk = "00011000011010100000" then 
				--C1
				Col<= "0111";
				sclk <= sclk+1;			-- check row pins
			elsif sclk = "00011000011010101000" then	
				--R1
				if Row = "0111" then
					DecodeOut <= "0001";	--1
				--R2
				elsif Row = "1011" then
					DecodeOut <= "0100"; --4
				--R3
				elsif Row = "1101" then
					DecodeOut <= "0111"; --7
				--R4
				elsif Row = "1110" then
					DecodeOut <= "0000"; --0
				end if;
				sclk <= sclk+1;
			-- 2ms
			elsif sclk = "00110000110101000000" then	
				--C2
				Col<= "1011";
				sclk <= sclk+1;
			-- check row pins
			elsif sclk = "00110000110101001000" then	
				--R1
				if Row = "0111" then		
					DecodeOut <= "0010"; --2
				--R2
				elsif Row = "1011" then
					DecodeOut <= "0101"; --5
				--R3
				elsif Row = "1101" then
					DecodeOut <= "1000"; --8
				--R4
				elsif Row = "1110" then
					DecodeOut <= "1111"; --F
				end if;
				sclk <= sclk+1;	
			--3ms
			elsif sclk = "01001001001111100000" then 
				--C3
				Col<= "1101";
				sclk <= sclk+1;
			-- check row pins
			elsif sclk = "01001001001111101000" then 
				--R1
				if Row = "0111" then
					DecodeOut <= "0011"; --3	
				--R2
				elsif Row = "1011" then
					DecodeOut <= "0110"; --6
				--R3
				elsif Row = "1101" then
					DecodeOut <= "1001"; --9
				--R4
				elsif Row = "1110" then
					DecodeOut <= "1110"; --E
				end if;
				sclk <= sclk+1;
			--4ms
			elsif sclk = "01100001101010000000" then 			
				--C4
				Col<= "1110";
				sclk <= sclk+1;
			-- check row pins
			elsif sclk = "01100001101010001000" then 
				--R1
				if Row = "0111" then
					DecodeOut <= "1010"; --A
				--R2
				elsif Row = "1011" then
					DecodeOut <= "1011"; --B
				--R3
				elsif Row = "1101" then
					DecodeOut <= "1100"; --C
				--R4
				elsif Row = "1110" then
					DecodeOut <= "1101"; --D
				end if;
				sclk <= "00000000000000000000";	
			else
				sclk <= sclk+1;	
			end if;
		end if;
	end process;
		
		
						 
end Behavioral;

// VHDL entity concanator, as the project stores it:
--------------------------------------------------------------------------------
-- Project :
-- File    :
-- Autor   :
-- Date    :
--
--------------------------------------------------------------------------------
-- Description :
--
--------------------------------------------------------------------------------

LIBRARY ieee;
USE ieee.std_logic_1164.all;

ENTITY concanator IS
  PORT (
 REG1:IN STD_LOGIC_VECTOR(3 DOWNTO 0);
 REG2: IN STD_LOGIC_VECTOR(3 DOWNTO 0);
 REG3:IN STD_LOGIC_VECTOR(3 DOWNTO 0);
 CLK : IN STD_LOGIC;
 OUTPUT_REG:OUT STD_LOGIC_VECTOR(15 DOWNTO 0)
    );
END concanator;

ARCHITECTURE TypeArchitecture OF concanator IS

BEGIN
	PROCESS(CLK)
	BEGIN
	IF RISING_EDGE( CLK) THEN
	OUTPUT_REG<="0000" & REG1 & REG2 & REG3;
	END IF;
	END PROCESS;

END TypeArchitecture;

// VHDL entity NUMARATOR4, as the project stores it:
LIBRARY ieee;
USE ieee.std_logic_1164.all;
USE ieee.std_logic_unsigned.all;

ENTITY NUMARATOR4 IS
  PORT (
  	CLK, RST, EN : IN STD_LOGIC;
  	Q : OUT STD_LOGIC_VECTOR( 3 DOWNTO 0)
    );
END NUMARATOR4;


ARCHITECTURE TypeArchitecture OF NUMARATOR4 IS

BEGIN

	PROCESS(CLK,RST,EN)
	VARIABLE NR: STD_LOGIC_VECTOR(3 DOWNTO 0):=(OTHERS => '0');
	BEGIN
		IF RST='1' THEN NR:=(OTHERS => '0');
		ELSIF RISING_EDGE( CLK ) THEN
			IF EN = '1' THEN 
			 	NR:= NR+1;
			END IF;
		END IF;
		Q <= NR;
	END PROCESS;

END TypeArchitecture;

// VHDL entity REG_MARE, as the project stores it:
LIBRARY ieee;
USE ieee.std_logic_1164.all;

ENTITY REG_MARE IS
  PORT (
  	V_IN : IN STD_LOGIC_VECTOR(15 DOWNTO 0);
  	EN : IN STD_LOGIC;
  	CLK : IN STD_LOGIC;
  	V_OUT : OUT STD_LOGIC_VECTOR(15 DOWNTO 0)
    );
END REG_MARE;

ARCHITECTURE TypeArchitecture OF REG_MARE IS

	SIGNAL V_INT : STD_LOGIC_VECTOR(15 DOWNTO 0);
BEGIN
	PROCESS(CLK)
	BEGIN
	IF RISING_EDGE(CLK) THEN 
		IF EN = '1' THEN
		V_INT <=  V_IN;
		END IF;
	END IF;  

	END PROCESS;
	V_OUT <= V_INT;
END TypeArchitecture;

// VHDL entity DMUX_2, as the project stores it:
library IEEE;
use IEEE.STD_LOGIC_1164.ALL;

entity DMUX_2 is
 port(
 		out0, out1:out std_logic_vector(15 downto 0);
       intr:in std_logic_vector(15 downto 0);
       sel:in std_logic
       );
end DMUX_2;

architecture Behavioral of DMUX_2 is

begin
	process(intr,sel)
    begin
    if(sel='0')then out0<=intr; --out1 <= "0000"; out2 <= "0000"; out3 <= "0000";
    elsif(sel='1')then out1<=intr; --out0<= "0000"; out2 <= "0000"; out3 <= "0000";
  end if;    
    end process;
end Behavioral;

// VHDL entity UC, as the project stores it:
LIBRARY ieee;
USE ieee.std_logic_1164.all;

ENTITY UC IS
  PORT (
  	ADMIN : IN STD_LOGIC;
	CIF1, CIF2, CIF3 : IN STD_LOGIC;
	CONFIRM : IN STD_LOGIC;
	CLK :IN STD_LOGIC;
	SEL: OUT STD_LOGIC;
	EN1, EN2, EN3: OUT STD_LOGIC
    );
END UC;

ARCHITECTURE TypeArchitecture OF UC IS

BEGIN
	PROCESS(CIF1, CIF2, CIF3, CONFIRM,CLK)
	BEGIN
		IF RISING_EDGE(CLK) THEN
		IF ADMIN = '1' THEN
			SEL <= '1';
		ELSIF CONFIRM = '1' THEN 
		SEL <= '1';
		ELSE SEL <= '0';
		END IF;
		IF CIF1 = '1' THEN 
			EN1 <= '1';
		ELSIF CIF2 = '1' THEN
			EN2 <= '1';
		ELSIF CIF3 = '1' THEN
			EN3 <= '1';
		ELSE EN1<='0'; EN2<='0'; EN3<='0';
		END IF;
		END IF; 	
	END PROCESS;	

END TypeArchitecture;

// VHDL entity T_FF, as the project stores it:
library IEEE;
use IEEE.STD_LOGIC_1164.ALL;
 
entity T_FF is
port( T: in std_logic;
RST : IN STD_LOGIC;
Q: out std_logic);
end T_FF;
 
architecture Behavioral of T_FF is
signal tmp: std_logic := '0';
begin
process (T,RST)
begin
IF RST = '1' THEN
tmp <= '0';
elsif T='0' then
tmp <= tmp;
elsif T='1' then
tmp <= not (tmp);
end if;
end process;
Q <= tmp;
end Behavioral;

// VHDL entity REG, as the project stores it:
LIBRARY ieee;
USE ieee.std_logic_1164.all;

ENTITY REG IS
  PORT (
  	V_IN : IN STD_LOGIC;
  	RST : IN STD_LOGIC;
  	CLK : IN STD_LOGIC;
  	V_OUT : OUT STD_LOGIC
    );
END REG;

ARCHITECTURE TypeArchitecture OF REG IS

	SIGNAL V_INT : STD_LOGIC := '0';
BEGIN
	PROCESS(V_IN,CLK)
	BEGIN
	IF RST = '1' THEN
		V_INT <= '0';
	ELSIF RISING_EDGE( CLK) THEN
		IF V_IN = '1' THEN 
		V_INT <=  V_IN;
	END IF;  
	END IF;
	END PROCESS;
	V_OUT <= V_INT;
END TypeArchitecture;

// VHDL entity DEB_3, as the project stores it:
LIBRARY ieee;
USE ieee.std_logic_1164.all;
USE ieee.std_logic_unsigned.all;

ENTITY DEB_3 IS
  PORT (
  CLK,B: IN STD_LOGIC;
	Y: OUT STD_LOGIC);
END DEB_3;

ARCHITECTURE STRUCT OF DEB_3 IS
COMPONENT BIS_D IS
  PORT (
CLK,D: IN STD_LOGIC;
  	Q: OUT STD_LOGIC);
END COMPONENT;
SIGNAL N1,N2: STD_LOGIC := '0';
BEGIN
C1: BIS_D PORT MAP (CLK,B,N1);
C2: BIS_D PORT MAP (CLK,N1,N2);
Y<= N1 AND N2;
END STRUCT;



LIBRARY ieee;
USE ieee.std_logic_1164.all;

USE ieee.std_logic_unsigned.all;

ENTITY BIS_D IS
  PORT (
CLK,D: IN STD_LOGIC;
  	Q: OUT STD_LOGIC);
END BIS_D;

ARCHITECTURE COMP OF BIS_D IS
BEGIN
PROCESS(CLK)
BEGIN
IF RISING_EDGE(CLK) THEN
	 Q<=D;
END IF;
END PROCESS;
END COMP;

// VHDL entity REG_ADMIN, as the project stores it:
LIBRARY ieee;
USE ieee.std_logic_1164.all;

ENTITY REG_ADMIN IS
  PORT (
  	V_OUT : OUT STD_LOGIC_VECTOR(15 DOWNTO 0)
    );
END REG_ADMIN;

ARCHITECTURE TypeArchitecture OF REG_ADMIN IS

BEGIN
	
	V_OUT <= "0000001100000001";
END TypeArchitecture;

// VHDL entity BIS_D, as the project stores it:
LIBRARY ieee;
USE ieee.std_logic_1164.all;

USE ieee.std_logic_unsigned.all;

ENTITY BIS_D IS
  PORT (
CLK,D: IN STD_LOGIC;
  	Q: OUT STD_LOGIC);
END BIS_D;

ARCHITECTURE COMP OF BIS_D IS
BEGIN
PROCESS(CLK)
BEGIN
IF RISING_EDGE(CLK) THEN
	 Q<=D;
END IF;
END PROCESS;
END COMP;

// VHDL entity ssd, as the project stores it:
library ieee;
use ieee.std_logic_1164.all;

entity ssd is
Port ( B0,B1,B2,B3 : in STD_LOGIC;
A,B,C,D,E,F,G : out STD_LOGIC);
end ssd;
 
architecture Behavioral of ssd is
 SIGNAL AS,BS,CS,DS,ES,FS,GS : STD_LOGIC := '0';
begin
 
AS <= B0 OR B2 OR (B1 AND B3) OR (NOT B1 AND NOT B3);
BS <= (NOT B1) OR (NOT B2 AND NOT B3) OR (B2 AND B3);
CS <= B1 OR NOT B2 OR B3;
DS <= (NOT B1 AND NOT B3) OR (B2 AND NOT B3) OR (B1 AND NOT B2 AND B3) OR (NOT B1 AND B2) OR B0;
ES <= (NOT B1 AND NOT B3) OR (B2 AND NOT B3);
FS <= B0 OR (NOT B2 AND NOT B3) OR (B1 AND NOT B2) OR (B1 AND NOT B3);
GS <= B0 OR (B1 AND NOT B2) OR ( NOT B1 AND B2) OR (B2 AND NOT B3);
A<=AS;
B<=BS;
C<=CS;
D<=DS;
E<=ES;
F<=FS;
G<=GS;
end architecture;

// VHDL entity ssd16, as the project stores it:
library IEEE;
use IEEE.STD_LOGIC_1164.ALL;
use IEEE.std_logic_unsigned.all;
entity ssd16 is
    Port ( clock_100Mhz : in STD_LOGIC;
           reset : in STD_LOGIC; 
           data: in std_logic_vector(15 downto 0);
           Anode_Activate : out STD_LOGIC_VECTOR (3 downto 0);
           LED_out : out STD_LOGIC_VECTOR (6 downto 0));
end ssd16;

architecture Behavioral of ssd16 is
signal one_second_counter: STD_LOGIC_VECTOR (27 downto 0);
signal one_second_enable: std_logic;
signal displayed_number: STD_LOGIC_VECTOR (15 downto 0);
signal LED_BCD: STD_LOGIC_VECTOR (3 downto 0);
signal refresh_counter: STD_LOGIC_VECTOR (19 downto 0);
signal LED_activating_counter: std_logic_vector(1 downto 0);

begin

process(LED_BCD)
begin
    case LED_BCD is
    when "0000" => LED_out <=	not "0000001"; -- "0"     
    when "0001" => LED_out <= not "1001111"; -- "1" 
    when "0010" => LED_out <= not "0010010"; -- "2" 
    when "0011" => LED_out <= not "0000110"; -- "3" 
    when "0100" => LED_out <= not "1001100"; -- "4" 
    when "0101" => LED_out <= not "0100100"; -- "5" 
    when "0110" => LED_out <= not "0100000"; -- "6" 
    when "0111" => LED_out <= not "0001111"; -- "7" 
    when "1000" => LED_out <= not "0000000"; -- "8"     
    when "1001" => LED_out <= not "0000100"; -- "9" 
    when "1010" => LED_out <= not "0000010"; -- a
    when "1011" => LED_out <= not "1100000"; -- b
    when "1100" => LED_out <= not "0110001"; -- C
    when "1101" => LED_out <= not "1000010"; -- d
    when "1110" => LED_out <= not "0110000"; -- E
    when "1111" => LED_out <= not "0111000"; -- F
    when others=> LED_out<= not"0000000";
    end case;
end process;

process(clock_100Mhz,reset)
begin 
    if(reset='1') then
        refresh_counter <= (others => '0');
    elsif(rising_edge(clock_100Mhz)) then
        refresh_counter <= refresh_counter + 1;
    end if;
end process;
 LED_activating_counter <= refresh_counter(19 downto 18);

process(LED_activating_counter)
begin
    case LED_activating_counter is
    when "00" =>
        Anode_Activate <= not "0111"; 
     
        LED_BCD <= displayed_number(15 downto 12);
        
    when "01" =>
        Anode_Activate <= not "1011"; 
       
        LED_BCD <= displayed_number(11 downto 8);
        
    when "10" =>
        Anode_Activate <= not "1101"; 
     
        LED_BCD <= displayed_number(7 downto 4);
        
    when "11" =>
        Anode_Activate <=not  "1110"; 
    
        LED_BCD <= displayed_number(3 downto 0);
       
        when others=>
        Anode_Activate <=not  "0000"; 
        
        LED_BCD <= not "0000";
       
            
    end case;
end process;
one_second_enable <= '1' ;
process(clock_100Mhz, reset)
begin
        if(reset='1') then
            displayed_number <= (others => '0');
        elsif(rising_edge(clock_100Mhz)) then
             if(one_second_enable='1') then
                displayed_number <= data ;
             end if;
        end if;
end process;
end Behavioral;

// VHDL entity clk_div, as the project stores it:
--------------------------------------------------------------------------------
-- Project :
-- File    :
-- Autor   :
-- Date    :
--
--------------------------------------------------------------------------------
-- Description :
--
--------------------------------------------------------------------------------

LIBRARY ieee;
USE ieee.std_logic_1164.all;

ENTITY clk_div IS
  PORT (
clk:in std_logic;
  clk_out:out std_logic
  
    );
END clk_div;



ARCHITECTURE TypeArchitecture OF clk_div IS

signal counter:integer:=1;
signal tmp:std_logic:='0';

BEGIN

	process(clk)
begin
if rising_edge(clk) then
counter<=counter+1;
if counter=50000000 then
tmp<=not tmp;
counter<=1;
end if;
end if;
clk_out<=tmp;
end process;

	

END TypeArchitecture;
